// Logisim project tp1.circ as structural Verilog: 27 circuits, main circuit main
module main (
);

  wire branch_1_out_4, Clk, Disp, IP_sel, Reg_WE, ULA_mux, Zero;
  wire [2:0] ULA_sel;
  wire [3:0] and_1_out_2, and_1_out_3, and_1_out_4, and_1_out_5, and_1_out_6;
  wire [11:0] and_1_out;
  wire [31:0] banco_registradores_1_a, banco_registradores_1_b, bit_extender_1_out, ext_16_32_1_out_2,
       ip_1_s, multiplexer_1_out, multiplexer_2_out, rom_1_data, somador_1_c, ula_1_c;

  Multiplexer #(.width(32)) multiplexer_1 (
    .in0(32'h1), .in1(ext_16_32_1_out_2), .out(multiplexer_1_out), .sel(branch_1_out_4));
  Branch branch_1 (.IP(IP_sel), .Zero(Zero), .Reg_WE(Reg_WE), .out_4(branch_1_out_4));
  ext_16_32 ext_16_32_1 (.in_1(rom_1_data[15:0]), .out_2(ext_16_32_1_out_2));
  Clock clock_1 (.out(Clk));
  Somador somador_1 (.A(ip_1_s), .B(multiplexer_1_out), .C(somador_1_c));
  IP ip_1 (.A(somador_1_c), .Clock(Clk), .S(ip_1_s));
  ROM #(.addrWidth(24), .dataWidth(32)) rom_1 (.addr(ip_1_s[23:0]), .data(rom_1_data));
  ROM #(.addrWidth(4), .dataWidth(7)) rom_2 (.addr(rom_1_data[31:28]), .data({ULA_mux, ULA_sel, Reg_WE, Disp, IP_sel}));
  Hex_Digit_Display hex_digit_display_1 (.value(and_1_out_6));  // open: dp
  Hex_Digit_Display hex_digit_display_2 (.value(and_1_out_5));  // open: dp
  Hex_Digit_Display hex_digit_display_3 (.value(and_1_out_4));  // open: dp
  Hex_Digit_Display hex_digit_display_4 (.value(and_1_out_3));  // open: dp
  Hex_Digit_Display hex_digit_display_5 (.value(and_1_out_2));  // open: dp
  Hex_Digit_Display hex_digit_display_6 (.value(and_1_out[11:8]));  // open: dp
  assign {and_1_out_6, and_1_out_5, and_1_out_4, and_1_out_3, and_1_out_2, and_1_out} = bit_extender_1_out & banco_registradores_1_a;  // AND_Gate and_1, 32 bits wide
  assign bit_extender_1_out = {{31{Disp}}, Disp};  // Bit_Extender bit_extender_1
  Banco_Registradores banco_registradores_1 (
    .a_in(rom_1_data[27:24]), .b_in(rom_1_data[23:20]), .c_in(rom_1_data[19:16]), .DATA(ula_1_c),
    .WE(Reg_WE), .Clock(Clk), .A(banco_registradores_1_a), .B(banco_registradores_1_b));
  Multiplexer #(.width(32)) multiplexer_2 (
    .in0(banco_registradores_1_b), .in1({{16{1'b0}}, rom_1_data[15:0]}), .out(multiplexer_2_out),
    .sel(ULA_mux));
  Hex_Digit_Display hex_digit_display_7 (.value(and_1_out[7:4]));  // open: dp
  Hex_Digit_Display hex_digit_display_8 (.value(and_1_out[3:0]));  // open: dp
  ULA ula_1 (.A(banco_registradores_1_a), .B(multiplexer_2_out), .Sel(ULA_sel), .C(ula_1_c), .Zero(Zero));

  // Notes on the sheet:
  //   contents of rom_1 (hex, n*v repeats v):
  //   0 b0010002 c1000000 b0020003 c2000000 11230000 c3000000 22140000 c4000000 31450000 41460000 51470000
  //   62080000 72490000 c9000000 824a0000 ca000000 920b0003 a20c0003 b20d0002 cd000000 d000000a e55e000a
  //   f0000000
  //   contents of rom_2 (hex, n*v repeats v):
  //   0 4 c 14 1c 24 2c 34 3c 5c 64 44 2 1 d 1
endmodule

module Banco_Registradores (
  input  [3:0] a_in,
  input  [3:0] b_in,
  input  [3:0] c_in,
  input  [31:0] DATA,
  input  WE,
  input  Clock,
  output [31:0] A,
  output [31:0] B
);

  wire demultiplexer_1_out0, demultiplexer_1_out1, demultiplexer_1_out2, demultiplexer_1_out3,
       demultiplexer_1_out4, demultiplexer_1_out5, demultiplexer_1_out6, demultiplexer_1_out7,
       demultiplexer_1_out8, demultiplexer_1_out9, demultiplexer_1_out10, demultiplexer_1_out11,
       demultiplexer_1_out12, demultiplexer_1_out13, demultiplexer_1_out14, demultiplexer_1_out15;
  wire [31:0] register_1_q, register_2_q, register_3_q, register_4_q, register_5_q, register_6_q,
       register_7_q, register_8_q, register_9_q, register_10_q, register_11_q, register_12_q, register_13_q,
       register_14_q, register_15_q, register_16_q;

  Demultiplexer #(.select(4)) demultiplexer_1 (
    .out0(demultiplexer_1_out0), .out1(demultiplexer_1_out1), .out2(demultiplexer_1_out2),
    .out3(demultiplexer_1_out3), .out4(demultiplexer_1_out4), .out5(demultiplexer_1_out5),
    .out6(demultiplexer_1_out6), .out7(demultiplexer_1_out7), .out8(demultiplexer_1_out8),
    .out9(demultiplexer_1_out9), .out10(demultiplexer_1_out10), .out11(demultiplexer_1_out11),
    .out12(demultiplexer_1_out12), .out13(demultiplexer_1_out13), .out14(demultiplexer_1_out14),
    .out15(demultiplexer_1_out15), .in(WE), .sel(c_in));
  Register #(.width(32)) register_1 (.D(DATA), .en(demultiplexer_1_out0), .clk(Clock), .Q(register_1_q));  // open: clr
  Register #(.width(32)) register_2 (.D(DATA), .en(demultiplexer_1_out1), .clk(Clock), .Q(register_2_q));  // open: clr
  Register #(.width(32)) register_3 (.D(DATA), .en(demultiplexer_1_out2), .clk(Clock), .Q(register_3_q));  // open: clr
  Register #(.width(32)) register_4 (.D(DATA), .en(demultiplexer_1_out3), .clk(Clock), .Q(register_4_q));  // open: clr
  Register #(.width(32)) register_5 (.D(DATA), .en(demultiplexer_1_out4), .clk(Clock), .Q(register_5_q));  // open: clr
  Register #(.width(32)) register_6 (.D(DATA), .en(demultiplexer_1_out5), .clk(Clock), .Q(register_6_q));  // open: clr
  Register #(.width(32)) register_7 (.D(DATA), .en(demultiplexer_1_out6), .clk(Clock), .Q(register_7_q));  // open: clr
  Register #(.width(32)) register_8 (.D(DATA), .en(demultiplexer_1_out7), .clk(Clock), .Q(register_8_q));  // open: clr
  Register #(.width(32)) register_9 (.D(DATA), .en(demultiplexer_1_out8), .clk(Clock), .Q(register_9_q));  // open: clr
  Register #(.width(32)) register_10 (
    .D(DATA), .en(demultiplexer_1_out9), .clk(Clock), .Q(register_10_q));  // open: clr
  Register #(.width(32)) register_11 (
    .D(DATA), .en(demultiplexer_1_out10), .clk(Clock), .Q(register_11_q));  // open: clr
  Register #(.width(32)) register_12 (
    .D(DATA), .en(demultiplexer_1_out11), .clk(Clock), .Q(register_12_q));  // open: clr
  Register #(.width(32)) register_13 (
    .D(DATA), .en(demultiplexer_1_out12), .clk(Clock), .Q(register_13_q));  // open: clr
  Register #(.width(32)) register_14 (
    .D(DATA), .en(demultiplexer_1_out13), .clk(Clock), .Q(register_14_q));  // open: clr
  Register #(.width(32)) register_15 (
    .D(DATA), .en(demultiplexer_1_out14), .clk(Clock), .Q(register_15_q));  // open: clr
  Register #(.width(32)) register_16 (
    .D(DATA), .en(demultiplexer_1_out15), .clk(Clock), .Q(register_16_q));  // open: clr
  Multiplexer #(.select(4), .width(32)) multiplexer_1 (
    .in0(register_1_q), .in1(register_2_q), .in2(register_3_q), .in3(register_4_q), .in4(register_5_q),
    .in5(register_6_q), .in6(register_7_q), .in7(register_8_q), .in8(register_9_q), .in9(register_10_q),
    .in10(register_11_q), .in11(register_12_q), .in12(register_13_q), .in13(register_14_q),
    .in14(register_15_q), .in15(register_16_q), .out(A), .sel(a_in));
  Multiplexer #(.select(4), .width(32)) multiplexer_2 (
    .in0(register_1_q), .in1(register_2_q), .in2(register_3_q), .in3(register_4_q), .in4(register_5_q),
    .in5(register_6_q), .in6(register_7_q), .in7(register_8_q), .in8(register_9_q), .in9(register_10_q),
    .in10(register_11_q), .in11(register_12_q), .in12(register_13_q), .in13(register_14_q),
    .in14(register_15_q), .in15(register_16_q), .out(B), .sel(b_in));
endmodule

module ULA (
  input  [31:0] A,
  input  [31:0] B,
  input  [2:0] Sel,
  output [31:0] C,
  output Zero
);

  wire [31:0] op_and_1_c, op_not_1_c, op_or_1_c, op_xor_1_c, shifter_l_1_c, shifter_r_1_c, somador_1_c,
       subtrator_1_c;

  Somador somador_1 (.A(A), .B(B), .C(somador_1_c));
  Subtrator subtrator_1 (.A(A), .B(B), .C(subtrator_1_c));
  op_AND op_and_1 (.A(A), .B(B), .C(op_and_1_c));
  op_OR op_or_1 (.A(A), .B(B), .C(op_or_1_c));
  op_XOR op_xor_1 (.A(A), .B(B), .C(op_xor_1_c));
  op_NOT op_not_1 (.A(A), .C(op_not_1_c));
  Shifter_L shifter_l_1 (.A(A), .B(B), .C(shifter_l_1_c));
  Shifter_R shifter_r_1 (.A(A), .B(B), .C(shifter_r_1_c));
  Multiplexer #(.select(3), .width(32)) multiplexer_1 (
    .in0(somador_1_c), .in1(subtrator_1_c), .in2(op_and_1_c), .in3(op_or_1_c), .in4(op_xor_1_c),
    .in5(op_not_1_c), .in6(shifter_l_1_c), .in7(shifter_r_1_c), .out(C), .sel(Sel));
  nor nor_1 (Zero, C[31], C[30], C[29], C[28], C[27], C[26], C[25], C[24], C[23], C[22], C[21], C[20], C[19], C[18], C[17], C[16], C[15], C[14], C[13], C[12], C[11], C[10], C[9], C[8], C[7], C[6], C[5], C[4], C[3], C[2], C[1], C[0]);

  // Other names for the same wires on the sheet: Seletor[2:0] = Sel
endmodule

module Somador (
  input  [31:0] A,
  input  [31:0] B,
  output [31:0] C
);

  wire adder_4bits_la_1_c_out, adder_4bits_la_2_c_out, adder_4bits_la_3_c_out, adder_4bits_la_4_c_out,
       adder_4bits_la_5_c_out, adder_4bits_la_6_c_out, adder_4bits_la_7_c_out, adder_4bits_la_8_c_out;

  Adder_4bits_LA adder_4bits_la_1 (.C_in(1'b0), .A(A[3:0]), .B(B[3:0]), .C_out(adder_4bits_la_1_c_out), .S(C[3:0]));
  Adder_4bits_LA adder_4bits_la_2 (
    .C_in(adder_4bits_la_7_c_out), .A(A[19:16]), .B(B[19:16]), .C_out(adder_4bits_la_2_c_out), .S(C[19:16]));
  Adder_4bits_LA adder_4bits_la_3 (
    .C_in(adder_4bits_la_1_c_out), .A(A[7:4]), .B(B[7:4]), .C_out(adder_4bits_la_3_c_out), .S(C[7:4]));
  Adder_4bits_LA adder_4bits_la_4 (
    .C_in(adder_4bits_la_2_c_out), .A(A[23:20]), .B(B[23:20]), .C_out(adder_4bits_la_4_c_out), .S(C[23:20]));
  Adder_4bits_LA adder_4bits_la_5 (
    .C_in(adder_4bits_la_3_c_out), .A(A[11:8]), .B(B[11:8]), .C_out(adder_4bits_la_5_c_out), .S(C[11:8]));
  Adder_4bits_LA adder_4bits_la_6 (
    .C_in(adder_4bits_la_4_c_out), .A(A[27:24]), .B(B[27:24]), .C_out(adder_4bits_la_6_c_out), .S(C[27:24]));
  Adder_4bits_LA adder_4bits_la_7 (
    .C_in(adder_4bits_la_5_c_out), .A(A[15:12]), .B(B[15:12]), .C_out(adder_4bits_la_7_c_out), .S(C[15:12]));
  Adder_4bits_LA adder_4bits_la_8 (
    .C_in(adder_4bits_la_6_c_out), .A(A[31:28]), .B(B[31:28]), .C_out(adder_4bits_la_8_c_out), .S(C[31:28]));
  // also tied to GND on the sheet: adder_4bits_la_8_c_out
endmodule

module Subtrator (
  input  [31:0] A,
  input  [31:0] B,
  output [31:0] C
);

  wire adder_4bits_la_1_c_out, adder_4bits_la_2_c_out, adder_4bits_la_3_c_out, adder_4bits_la_4_c_out,
       adder_4bits_la_5_c_out, adder_4bits_la_6_c_out, adder_4bits_la_7_c_out;
  wire [31:0] not_1_out;

  assign not_1_out = ~B;  // NOT_Gate not_1, 32 bits wide
  Adder_4bits_LA adder_4bits_la_1 (
    .C_in(1'b1), .A(A[3:0]), .B(not_1_out[3:0]), .C_out(adder_4bits_la_1_c_out), .S(C[3:0]));
  Adder_4bits_LA adder_4bits_la_2 (
    .C_in(adder_4bits_la_7_c_out), .A(A[19:16]), .B(not_1_out[19:16]), .C_out(adder_4bits_la_2_c_out),
    .S(C[19:16]));
  Adder_4bits_LA adder_4bits_la_3 (
    .C_in(adder_4bits_la_1_c_out), .A(A[7:4]), .B(not_1_out[7:4]), .C_out(adder_4bits_la_3_c_out), .S(C[7:4]));
  Adder_4bits_LA adder_4bits_la_4 (
    .C_in(adder_4bits_la_2_c_out), .A(A[23:20]), .B(not_1_out[23:20]), .C_out(adder_4bits_la_4_c_out),
    .S(C[23:20]));
  Adder_4bits_LA adder_4bits_la_5 (
    .C_in(adder_4bits_la_3_c_out), .A(A[11:8]), .B(not_1_out[11:8]), .C_out(adder_4bits_la_5_c_out),
    .S(C[11:8]));
  Adder_4bits_LA adder_4bits_la_6 (
    .C_in(adder_4bits_la_4_c_out), .A(A[27:24]), .B(not_1_out[27:24]), .C_out(adder_4bits_la_6_c_out),
    .S(C[27:24]));
  Adder_4bits_LA adder_4bits_la_7 (
    .C_in(adder_4bits_la_5_c_out), .A(A[15:12]), .B(not_1_out[15:12]), .C_out(adder_4bits_la_7_c_out),
    .S(C[15:12]));
  Adder_4bits_LA adder_4bits_la_8 (
    .C_in(adder_4bits_la_6_c_out), .A(A[31:28]), .B(not_1_out[31:28]), .S(C[31:28]));  // open: C_out
endmodule

module op_AND (
  input  [31:0] A,
  input  [31:0] B,
  output [31:0] C
);

  assign C = A & B;  // AND_Gate and_1, 32 bits wide
endmodule

module op_OR (
  input  [31:0] A,
  input  [31:0] B,
  output [31:0] C
);

  assign C = A | B;  // OR_Gate or_1, 32 bits wide
endmodule

module op_XOR (
  input  [31:0] A,
  input  [31:0] B,
  output [31:0] C
);

  assign C = A ^ B;  // XOR_Gate xor_1, 32 bits wide
endmodule

module op_NOT (
  input  [31:0] A,
  output [31:0] C
);

  assign C = ~A;  // NOT_Gate not_1, 32 bits wide
endmodule

module Shifter_L (
  input  [31:0] A,
  input  [31:0] B,
  output [31:0] C
);

  wire or_1_out;
  wire [31:0] shift_1bit_l_1_c, shift_2bit_l_1_c, shift_4bit_l_1_c, shift_8bit_l_1_c, shift_16bit_l_1_c;

  or or_1 (or_1_out, B[5], B[6], B[7], B[8], B[9], B[10], B[11], B[12], B[13], B[14], B[15], B[16], B[17], B[18], B[19], B[20], B[21], B[22], B[23], B[24], B[25], B[26], B[27], B[28], B[29], B[30], B[31]);
  Shift_1bit_L shift_1bit_l_1 (.A(A), .Bit_0(B[0]), .C(shift_1bit_l_1_c));
  Shift_2bit_L shift_2bit_l_1 (.A(shift_1bit_l_1_c), .Bit_1(B[1]), .C(shift_2bit_l_1_c));
  Shift_4bit_L shift_4bit_l_1 (.A(shift_2bit_l_1_c), .Bit_2(B[2]), .C(shift_4bit_l_1_c));
  Shift_8bit_L shift_8bit_l_1 (.A(shift_4bit_l_1_c), .Bit_3(B[3]), .C(shift_8bit_l_1_c));
  Shift_16bit_L shift_16bit_l_1 (.A(shift_8bit_l_1_c), .Bit_4(B[4]), .C(shift_16bit_l_1_c));
  Multiplexer #(.width(32)) multiplexer_1 (.in0(shift_16bit_l_1_c), .in1({32{1'b0}}), .out(C), .sel(or_1_out));
endmodule

module Shift_1bit_L (
  input  [31:0] A,
  input  Bit_0,
  output [31:0] C
);

  Multiplexer multiplexer_1 (.in0(A[31]), .in1(A[30]), .out(C[31]), .sel(Bit_0));
  Multiplexer multiplexer_2 (.in0(A[30]), .in1(A[29]), .out(C[30]), .sel(Bit_0));
  Multiplexer multiplexer_3 (.in0(A[29]), .in1(A[28]), .out(C[29]), .sel(Bit_0));
  Multiplexer multiplexer_4 (.in0(A[28]), .in1(A[27]), .out(C[28]), .sel(Bit_0));
  Multiplexer multiplexer_5 (.in0(A[27]), .in1(A[26]), .out(C[27]), .sel(Bit_0));
  Multiplexer multiplexer_6 (.in0(A[26]), .in1(A[25]), .out(C[26]), .sel(Bit_0));
  Multiplexer multiplexer_7 (.in0(A[25]), .in1(A[24]), .out(C[25]), .sel(Bit_0));
  Multiplexer multiplexer_8 (.in0(A[24]), .in1(A[23]), .out(C[24]), .sel(Bit_0));
  Multiplexer multiplexer_9 (.in0(A[23]), .in1(A[22]), .out(C[23]), .sel(Bit_0));
  Multiplexer multiplexer_10 (.in0(A[22]), .in1(A[21]), .out(C[22]), .sel(Bit_0));
  Multiplexer multiplexer_11 (.in0(A[21]), .in1(A[20]), .out(C[21]), .sel(Bit_0));
  Multiplexer multiplexer_12 (.in0(A[20]), .in1(A[19]), .out(C[20]), .sel(Bit_0));
  Multiplexer multiplexer_13 (.in0(A[19]), .in1(A[18]), .out(C[19]), .sel(Bit_0));
  Multiplexer multiplexer_14 (.in0(A[18]), .in1(A[17]), .out(C[18]), .sel(Bit_0));
  Multiplexer multiplexer_15 (.in0(A[17]), .in1(A[16]), .out(C[17]), .sel(Bit_0));
  Multiplexer multiplexer_16 (.in0(A[16]), .in1(A[15]), .out(C[16]), .sel(Bit_0));
  Multiplexer multiplexer_17 (.in0(A[15]), .in1(A[14]), .out(C[15]), .sel(Bit_0));
  Multiplexer multiplexer_18 (.in0(A[14]), .in1(A[13]), .out(C[14]), .sel(Bit_0));
  Multiplexer multiplexer_19 (.in0(A[13]), .in1(A[12]), .out(C[13]), .sel(Bit_0));
  Multiplexer multiplexer_20 (.in0(A[12]), .in1(A[11]), .out(C[12]), .sel(Bit_0));
  Multiplexer multiplexer_21 (.in0(A[11]), .in1(A[10]), .out(C[11]), .sel(Bit_0));
  Multiplexer multiplexer_22 (.in0(A[10]), .in1(A[9]), .out(C[10]), .sel(Bit_0));
  Multiplexer multiplexer_23 (.in0(A[9]), .in1(A[8]), .out(C[9]), .sel(Bit_0));
  Multiplexer multiplexer_24 (.in0(A[8]), .in1(A[7]), .out(C[8]), .sel(Bit_0));
  Multiplexer multiplexer_25 (.in0(A[7]), .in1(A[6]), .out(C[7]), .sel(Bit_0));
  Multiplexer multiplexer_26 (.in0(A[6]), .in1(A[5]), .out(C[6]), .sel(Bit_0));
  Multiplexer multiplexer_27 (.in0(A[5]), .in1(A[4]), .out(C[5]), .sel(Bit_0));
  Multiplexer multiplexer_28 (.in0(A[4]), .in1(A[3]), .out(C[4]), .sel(Bit_0));
  Multiplexer multiplexer_29 (.in0(A[3]), .in1(A[2]), .out(C[3]), .sel(Bit_0));
  Multiplexer multiplexer_30 (.in0(A[2]), .in1(A[1]), .out(C[2]), .sel(Bit_0));
  Multiplexer multiplexer_31 (.in0(A[1]), .in1(A[0]), .out(C[1]), .sel(Bit_0));
  Multiplexer multiplexer_32 (.in0(A[0]), .in1(1'b0), .out(C[0]), .sel(Bit_0));

  // Other names for the same wires on the sheet: S = Bit_0
endmodule

module Shift_2bit_L (
  input  [31:0] A,
  input  Bit_1,
  output [31:0] C
);

  Multiplexer multiplexer_1 (.in0(A[31]), .in1(A[29]), .out(C[31]), .sel(Bit_1));
  Multiplexer multiplexer_2 (.in0(A[30]), .in1(A[28]), .out(C[30]), .sel(Bit_1));
  Multiplexer multiplexer_3 (.in0(A[29]), .in1(A[27]), .out(C[29]), .sel(Bit_1));
  Multiplexer multiplexer_4 (.in0(A[28]), .in1(A[26]), .out(C[28]), .sel(Bit_1));
  Multiplexer multiplexer_5 (.in0(A[27]), .in1(A[25]), .out(C[27]), .sel(Bit_1));
  Multiplexer multiplexer_6 (.in0(A[26]), .in1(A[24]), .out(C[26]), .sel(Bit_1));
  Multiplexer multiplexer_7 (.in0(A[25]), .in1(A[23]), .out(C[25]), .sel(Bit_1));
  Multiplexer multiplexer_8 (.in0(A[24]), .in1(A[22]), .out(C[24]), .sel(Bit_1));
  Multiplexer multiplexer_9 (.in0(A[23]), .in1(A[21]), .out(C[23]), .sel(Bit_1));
  Multiplexer multiplexer_10 (.in0(A[22]), .in1(A[20]), .out(C[22]), .sel(Bit_1));
  Multiplexer multiplexer_11 (.in0(A[21]), .in1(A[19]), .out(C[21]), .sel(Bit_1));
  Multiplexer multiplexer_12 (.in0(A[20]), .in1(A[18]), .out(C[20]), .sel(Bit_1));
  Multiplexer multiplexer_13 (.in0(A[19]), .in1(A[17]), .out(C[19]), .sel(Bit_1));
  Multiplexer multiplexer_14 (.in0(A[18]), .in1(A[16]), .out(C[18]), .sel(Bit_1));
  Multiplexer multiplexer_15 (.in0(A[17]), .in1(A[15]), .out(C[17]), .sel(Bit_1));
  Multiplexer multiplexer_16 (.in0(A[16]), .in1(A[14]), .out(C[16]), .sel(Bit_1));
  Multiplexer multiplexer_17 (.in0(A[15]), .in1(A[13]), .out(C[15]), .sel(Bit_1));
  Multiplexer multiplexer_18 (.in0(A[14]), .in1(A[12]), .out(C[14]), .sel(Bit_1));
  Multiplexer multiplexer_19 (.in0(A[13]), .in1(A[11]), .out(C[13]), .sel(Bit_1));
  Multiplexer multiplexer_20 (.in0(A[12]), .in1(A[10]), .out(C[12]), .sel(Bit_1));
  Multiplexer multiplexer_21 (.in0(A[11]), .in1(A[9]), .out(C[11]), .sel(Bit_1));
  Multiplexer multiplexer_22 (.in0(A[10]), .in1(A[8]), .out(C[10]), .sel(Bit_1));
  Multiplexer multiplexer_23 (.in0(A[9]), .in1(A[7]), .out(C[9]), .sel(Bit_1));
  Multiplexer multiplexer_24 (.in0(A[8]), .in1(A[6]), .out(C[8]), .sel(Bit_1));
  Multiplexer multiplexer_25 (.in0(A[7]), .in1(A[5]), .out(C[7]), .sel(Bit_1));
  Multiplexer multiplexer_26 (.in0(A[6]), .in1(A[4]), .out(C[6]), .sel(Bit_1));
  Multiplexer multiplexer_27 (.in0(A[5]), .in1(A[3]), .out(C[5]), .sel(Bit_1));
  Multiplexer multiplexer_28 (.in0(A[4]), .in1(A[2]), .out(C[4]), .sel(Bit_1));
  Multiplexer multiplexer_29 (.in0(A[3]), .in1(A[1]), .out(C[3]), .sel(Bit_1));
  Multiplexer multiplexer_30 (.in0(A[2]), .in1(A[0]), .out(C[2]), .sel(Bit_1));
  Multiplexer multiplexer_31 (.in0(A[1]), .in1(1'b0), .out(C[1]), .sel(Bit_1));
  Multiplexer multiplexer_32 (.in0(A[0]), .in1(1'b0), .out(C[0]), .sel(Bit_1));

  // Other names for the same wires on the sheet: S = Bit_1
endmodule

module Shift_4bit_L (
  input  [31:0] A,
  input  Bit_2,
  output [31:0] C
);

  Multiplexer multiplexer_1 (.in0(A[31]), .in1(A[27]), .out(C[31]), .sel(Bit_2));
  Multiplexer multiplexer_2 (.in0(A[30]), .in1(A[26]), .out(C[30]), .sel(Bit_2));
  Multiplexer multiplexer_3 (.in0(A[29]), .in1(A[25]), .out(C[29]), .sel(Bit_2));
  Multiplexer multiplexer_4 (.in0(A[28]), .in1(A[24]), .out(C[28]), .sel(Bit_2));
  Multiplexer multiplexer_5 (.in0(A[27]), .in1(A[23]), .out(C[27]), .sel(Bit_2));
  Multiplexer multiplexer_6 (.in0(A[26]), .in1(A[22]), .out(C[26]), .sel(Bit_2));
  Multiplexer multiplexer_7 (.in0(A[25]), .in1(A[21]), .out(C[25]), .sel(Bit_2));
  Multiplexer multiplexer_8 (.in0(A[24]), .in1(A[20]), .out(C[24]), .sel(Bit_2));
  Multiplexer multiplexer_9 (.in0(A[23]), .in1(A[19]), .out(C[23]), .sel(Bit_2));
  Multiplexer multiplexer_10 (.in0(A[22]), .in1(A[18]), .out(C[22]), .sel(Bit_2));
  Multiplexer multiplexer_11 (.in0(A[21]), .in1(A[17]), .out(C[21]), .sel(Bit_2));
  Multiplexer multiplexer_12 (.in0(A[20]), .in1(A[16]), .out(C[20]), .sel(Bit_2));
  Multiplexer multiplexer_13 (.in0(A[19]), .in1(A[15]), .out(C[19]), .sel(Bit_2));
  Multiplexer multiplexer_14 (.in0(A[18]), .in1(A[14]), .out(C[18]), .sel(Bit_2));
  Multiplexer multiplexer_15 (.in0(A[17]), .in1(A[13]), .out(C[17]), .sel(Bit_2));
  Multiplexer multiplexer_16 (.in0(A[16]), .in1(A[12]), .out(C[16]), .sel(Bit_2));
  Multiplexer multiplexer_17 (.in0(A[15]), .in1(A[11]), .out(C[15]), .sel(Bit_2));
  Multiplexer multiplexer_18 (.in0(A[14]), .in1(A[10]), .out(C[14]), .sel(Bit_2));
  Multiplexer multiplexer_19 (.in0(A[13]), .in1(A[9]), .out(C[13]), .sel(Bit_2));
  Multiplexer multiplexer_20 (.in0(A[12]), .in1(A[8]), .out(C[12]), .sel(Bit_2));
  Multiplexer multiplexer_21 (.in0(A[11]), .in1(A[7]), .out(C[11]), .sel(Bit_2));
  Multiplexer multiplexer_22 (.in0(A[10]), .in1(A[6]), .out(C[10]), .sel(Bit_2));
  Multiplexer multiplexer_23 (.in0(A[9]), .in1(A[5]), .out(C[9]), .sel(Bit_2));
  Multiplexer multiplexer_24 (.in0(A[8]), .in1(A[4]), .out(C[8]), .sel(Bit_2));
  Multiplexer multiplexer_25 (.in0(A[7]), .in1(A[3]), .out(C[7]), .sel(Bit_2));
  Multiplexer multiplexer_26 (.in0(A[6]), .in1(A[2]), .out(C[6]), .sel(Bit_2));
  Multiplexer multiplexer_27 (.in0(A[5]), .in1(A[1]), .out(C[5]), .sel(Bit_2));
  Multiplexer multiplexer_28 (.in0(A[4]), .in1(A[0]), .out(C[4]), .sel(Bit_2));
  Multiplexer multiplexer_29 (.in0(A[3]), .in1(1'b0), .out(C[3]), .sel(Bit_2));
  Multiplexer multiplexer_30 (.in0(A[2]), .in1(1'b0), .out(C[2]), .sel(Bit_2));
  Multiplexer multiplexer_31 (.in0(A[1]), .in1(1'b0), .out(C[1]), .sel(Bit_2));
  Multiplexer multiplexer_32 (.in0(A[0]), .in1(1'b0), .out(C[0]), .sel(Bit_2));

  // Other names for the same wires on the sheet: S = Bit_2
endmodule

module Shift_8bit_L (
  input  [31:0] A,
  input  Bit_3,
  output [31:0] C
);

  Multiplexer multiplexer_1 (.in0(A[31]), .in1(A[23]), .out(C[31]), .sel(Bit_3));
  Multiplexer multiplexer_2 (.in0(A[30]), .in1(A[22]), .out(C[30]), .sel(Bit_3));
  Multiplexer multiplexer_3 (.in0(A[29]), .in1(A[21]), .out(C[29]), .sel(Bit_3));
  Multiplexer multiplexer_4 (.in0(A[28]), .in1(A[20]), .out(C[28]), .sel(Bit_3));
  Multiplexer multiplexer_5 (.in0(A[27]), .in1(A[19]), .out(C[27]), .sel(Bit_3));
  Multiplexer multiplexer_6 (.in0(A[26]), .in1(A[18]), .out(C[26]), .sel(Bit_3));
  Multiplexer multiplexer_7 (.in0(A[25]), .in1(A[17]), .out(C[25]), .sel(Bit_3));
  Multiplexer multiplexer_8 (.in0(A[24]), .in1(A[16]), .out(C[24]), .sel(Bit_3));
  Multiplexer multiplexer_9 (.in0(A[23]), .in1(A[15]), .out(C[23]), .sel(Bit_3));
  Multiplexer multiplexer_10 (.in0(A[22]), .in1(A[14]), .out(C[22]), .sel(Bit_3));
  Multiplexer multiplexer_11 (.in0(A[21]), .in1(A[13]), .out(C[21]), .sel(Bit_3));
  Multiplexer multiplexer_12 (.in0(A[20]), .in1(A[12]), .out(C[20]), .sel(Bit_3));
  Multiplexer multiplexer_13 (.in0(A[19]), .in1(A[11]), .out(C[19]), .sel(Bit_3));
  Multiplexer multiplexer_14 (.in0(A[18]), .in1(A[10]), .out(C[18]), .sel(Bit_3));
  Multiplexer multiplexer_15 (.in0(A[17]), .in1(A[9]), .out(C[17]), .sel(Bit_3));
  Multiplexer multiplexer_16 (.in0(A[16]), .in1(A[8]), .out(C[16]), .sel(Bit_3));
  Multiplexer multiplexer_17 (.in0(A[15]), .in1(A[7]), .out(C[15]), .sel(Bit_3));
  Multiplexer multiplexer_18 (.in0(A[14]), .in1(A[6]), .out(C[14]), .sel(Bit_3));
  Multiplexer multiplexer_19 (.in0(A[13]), .in1(A[5]), .out(C[13]), .sel(Bit_3));
  Multiplexer multiplexer_20 (.in0(A[12]), .in1(A[4]), .out(C[12]), .sel(Bit_3));
  Multiplexer multiplexer_21 (.in0(A[11]), .in1(A[3]), .out(C[11]), .sel(Bit_3));
  Multiplexer multiplexer_22 (.in0(A[10]), .in1(A[2]), .out(C[10]), .sel(Bit_3));
  Multiplexer multiplexer_23 (.in0(A[9]), .in1(A[1]), .out(C[9]), .sel(Bit_3));
  Multiplexer multiplexer_24 (.in0(A[8]), .in1(A[0]), .out(C[8]), .sel(Bit_3));
  Multiplexer multiplexer_25 (.in0(A[7]), .in1(1'b0), .out(C[7]), .sel(Bit_3));
  Multiplexer multiplexer_26 (.in0(A[6]), .in1(1'b0), .out(C[6]), .sel(Bit_3));
  Multiplexer multiplexer_27 (.in0(A[5]), .in1(1'b0), .out(C[5]), .sel(Bit_3));
  Multiplexer multiplexer_28 (.in0(A[4]), .in1(1'b0), .out(C[4]), .sel(Bit_3));
  Multiplexer multiplexer_29 (.in0(A[3]), .in1(1'b0), .out(C[3]), .sel(Bit_3));
  Multiplexer multiplexer_30 (.in0(A[2]), .in1(1'b0), .out(C[2]), .sel(Bit_3));
  Multiplexer multiplexer_31 (.in0(A[1]), .in1(1'b0), .out(C[1]), .sel(Bit_3));
  Multiplexer multiplexer_32 (.in0(A[0]), .in1(1'b0), .out(C[0]), .sel(Bit_3));

  // Other names for the same wires on the sheet: S = Bit_3
endmodule

module Shift_16bit_L (
  input  [31:0] A,
  input  Bit_4,
  output [31:0] C
);

  Multiplexer multiplexer_1 (.in0(A[31]), .in1(A[15]), .out(C[31]), .sel(Bit_4));
  Multiplexer multiplexer_2 (.in0(A[30]), .in1(A[14]), .out(C[30]), .sel(Bit_4));
  Multiplexer multiplexer_3 (.in0(A[29]), .in1(A[13]), .out(C[29]), .sel(Bit_4));
  Multiplexer multiplexer_4 (.in0(A[28]), .in1(A[12]), .out(C[28]), .sel(Bit_4));
  Multiplexer multiplexer_5 (.in0(A[27]), .in1(A[11]), .out(C[27]), .sel(Bit_4));
  Multiplexer multiplexer_6 (.in0(A[26]), .in1(A[10]), .out(C[26]), .sel(Bit_4));
  Multiplexer multiplexer_7 (.in0(A[25]), .in1(A[9]), .out(C[25]), .sel(Bit_4));
  Multiplexer multiplexer_8 (.in0(A[24]), .in1(A[8]), .out(C[24]), .sel(Bit_4));
  Multiplexer multiplexer_9 (.in0(A[23]), .in1(A[7]), .out(C[23]), .sel(Bit_4));
  Multiplexer multiplexer_10 (.in0(A[22]), .in1(A[6]), .out(C[22]), .sel(Bit_4));
  Multiplexer multiplexer_11 (.in0(A[21]), .in1(A[5]), .out(C[21]), .sel(Bit_4));
  Multiplexer multiplexer_12 (.in0(A[20]), .in1(A[4]), .out(C[20]), .sel(Bit_4));
  Multiplexer multiplexer_13 (.in0(A[19]), .in1(A[3]), .out(C[19]), .sel(Bit_4));
  Multiplexer multiplexer_14 (.in0(A[18]), .in1(A[2]), .out(C[18]), .sel(Bit_4));
  Multiplexer multiplexer_15 (.in0(A[17]), .in1(A[1]), .out(C[17]), .sel(Bit_4));
  Multiplexer multiplexer_16 (.in0(A[16]), .in1(A[0]), .out(C[16]), .sel(Bit_4));
  Multiplexer multiplexer_17 (.in0(A[15]), .in1(1'b0), .out(C[15]), .sel(Bit_4));
  Multiplexer multiplexer_18 (.in0(A[14]), .in1(1'b0), .out(C[14]), .sel(Bit_4));
  Multiplexer multiplexer_19 (.in0(A[13]), .in1(1'b0), .out(C[13]), .sel(Bit_4));
  Multiplexer multiplexer_20 (.in0(A[12]), .in1(1'b0), .out(C[12]), .sel(Bit_4));
  Multiplexer multiplexer_21 (.in0(A[11]), .in1(1'b0), .out(C[11]), .sel(Bit_4));
  Multiplexer multiplexer_22 (.in0(A[10]), .in1(1'b0), .out(C[10]), .sel(Bit_4));
  Multiplexer multiplexer_23 (.in0(A[9]), .in1(1'b0), .out(C[9]), .sel(Bit_4));
  Multiplexer multiplexer_24 (.in0(A[8]), .in1(1'b0), .out(C[8]), .sel(Bit_4));
  Multiplexer multiplexer_25 (.in0(A[7]), .in1(1'b0), .out(C[7]), .sel(Bit_4));
  Multiplexer multiplexer_26 (.in0(A[6]), .in1(1'b0), .out(C[6]), .sel(Bit_4));
  Multiplexer multiplexer_27 (.in0(A[5]), .in1(1'b0), .out(C[5]), .sel(Bit_4));
  Multiplexer multiplexer_28 (.in0(A[4]), .in1(1'b0), .out(C[4]), .sel(Bit_4));
  Multiplexer multiplexer_29 (.in0(A[3]), .in1(1'b0), .out(C[3]), .sel(Bit_4));
  Multiplexer multiplexer_30 (.in0(A[2]), .in1(1'b0), .out(C[2]), .sel(Bit_4));
  Multiplexer multiplexer_31 (.in0(A[1]), .in1(1'b0), .out(C[1]), .sel(Bit_4));
  Multiplexer multiplexer_32 (.in0(A[0]), .in1(1'b0), .out(C[0]), .sel(Bit_4));

  // Other names for the same wires on the sheet: S = Bit_4
endmodule

module Shifter_R (
  input  [31:0] A,
  input  [31:0] B,
  output [31:0] C
);

  wire or_1_out;
  wire [31:0] shift_1bit_r_1_c, shift_2bit_r_1_c, shift_4bit_r_1_c, shift_8bit_r_1_c, shift_16bit_r_1_c;

  or or_1 (or_1_out, B[5], B[6], B[7], B[8], B[9], B[10], B[11], B[12], B[13], B[14], B[15], B[16], B[17], B[18], B[19], B[20], B[21], B[22], B[23], B[24], B[25], B[26], B[27], B[28], B[29], B[30], B[31]);
  Shift_1bit_R shift_1bit_r_1 (.A(A), .Bit_0(B[0]), .C(shift_1bit_r_1_c));
  Shift_2bit_R shift_2bit_r_1 (.A(shift_1bit_r_1_c), .Bit_1(B[1]), .C(shift_2bit_r_1_c));
  Shift_4bit_R shift_4bit_r_1 (.A(shift_2bit_r_1_c), .Bit_2(B[2]), .C(shift_4bit_r_1_c));
  Shift_8bit_R shift_8bit_r_1 (.A(shift_4bit_r_1_c), .Bit_3(B[3]), .C(shift_8bit_r_1_c));
  Shift_16bit_R shift_16bit_r_1 (.A(shift_8bit_r_1_c), .Bit_4(B[4]), .C(shift_16bit_r_1_c));
  Multiplexer #(.width(32)) multiplexer_1 (.in0(shift_16bit_r_1_c), .in1({32{1'b0}}), .out(C), .sel(or_1_out));
endmodule

module Shift_1bit_R (
  input  [31:0] A,
  input  Bit_0,
  output [31:0] C
);

  Multiplexer multiplexer_1 (.in0(A[31]), .in1(1'b0), .out(C[31]), .sel(Bit_0));
  Multiplexer multiplexer_2 (.in0(A[30]), .in1(A[31]), .out(C[30]), .sel(Bit_0));
  Multiplexer multiplexer_3 (.in0(A[29]), .in1(A[30]), .out(C[29]), .sel(Bit_0));
  Multiplexer multiplexer_4 (.in0(A[28]), .in1(A[29]), .out(C[28]), .sel(Bit_0));
  Multiplexer multiplexer_5 (.in0(A[27]), .in1(A[28]), .out(C[27]), .sel(Bit_0));
  Multiplexer multiplexer_6 (.in0(A[26]), .in1(A[27]), .out(C[26]), .sel(Bit_0));
  Multiplexer multiplexer_7 (.in0(A[25]), .in1(A[26]), .out(C[25]), .sel(Bit_0));
  Multiplexer multiplexer_8 (.in0(A[24]), .in1(A[25]), .out(C[24]), .sel(Bit_0));
  Multiplexer multiplexer_9 (.in0(A[23]), .in1(A[24]), .out(C[23]), .sel(Bit_0));
  Multiplexer multiplexer_10 (.in0(A[22]), .in1(A[23]), .out(C[22]), .sel(Bit_0));
  Multiplexer multiplexer_11 (.in0(A[21]), .in1(A[22]), .out(C[21]), .sel(Bit_0));
  Multiplexer multiplexer_12 (.in0(A[20]), .in1(A[21]), .out(C[20]), .sel(Bit_0));
  Multiplexer multiplexer_13 (.in0(A[19]), .in1(A[20]), .out(C[19]), .sel(Bit_0));
  Multiplexer multiplexer_14 (.in0(A[18]), .in1(A[19]), .out(C[18]), .sel(Bit_0));
  Multiplexer multiplexer_15 (.in0(A[17]), .in1(A[18]), .out(C[17]), .sel(Bit_0));
  Multiplexer multiplexer_16 (.in0(A[16]), .in1(A[17]), .out(C[16]), .sel(Bit_0));
  Multiplexer multiplexer_17 (.in0(A[15]), .in1(A[16]), .out(C[15]), .sel(Bit_0));
  Multiplexer multiplexer_18 (.in0(A[14]), .in1(A[15]), .out(C[14]), .sel(Bit_0));
  Multiplexer multiplexer_19 (.in0(A[13]), .in1(A[14]), .out(C[13]), .sel(Bit_0));
  Multiplexer multiplexer_20 (.in0(A[12]), .in1(A[13]), .out(C[12]), .sel(Bit_0));
  Multiplexer multiplexer_21 (.in0(A[11]), .in1(A[12]), .out(C[11]), .sel(Bit_0));
  Multiplexer multiplexer_22 (.in0(A[10]), .in1(A[11]), .out(C[10]), .sel(Bit_0));
  Multiplexer multiplexer_23 (.in0(A[9]), .in1(A[10]), .out(C[9]), .sel(Bit_0));
  Multiplexer multiplexer_24 (.in0(A[8]), .in1(A[9]), .out(C[8]), .sel(Bit_0));
  Multiplexer multiplexer_25 (.in0(A[7]), .in1(A[8]), .out(C[7]), .sel(Bit_0));
  Multiplexer multiplexer_26 (.in0(A[6]), .in1(A[7]), .out(C[6]), .sel(Bit_0));
  Multiplexer multiplexer_27 (.in0(A[5]), .in1(A[6]), .out(C[5]), .sel(Bit_0));
  Multiplexer multiplexer_28 (.in0(A[4]), .in1(A[5]), .out(C[4]), .sel(Bit_0));
  Multiplexer multiplexer_29 (.in0(A[3]), .in1(A[4]), .out(C[3]), .sel(Bit_0));
  Multiplexer multiplexer_30 (.in0(A[2]), .in1(A[3]), .out(C[2]), .sel(Bit_0));
  Multiplexer multiplexer_31 (.in0(A[1]), .in1(A[2]), .out(C[1]), .sel(Bit_0));
  Multiplexer multiplexer_32 (.in0(A[0]), .in1(A[1]), .out(C[0]), .sel(Bit_0));

  // Other names for the same wires on the sheet: S = Bit_0
endmodule

module Shift_2bit_R (
  input  [31:0] A,
  input  Bit_1,
  output [31:0] C
);

  Multiplexer multiplexer_1 (.in0(A[31]), .in1(1'b0), .out(C[31]), .sel(Bit_1));
  Multiplexer multiplexer_2 (.in0(A[30]), .in1(1'b0), .out(C[30]), .sel(Bit_1));
  Multiplexer multiplexer_3 (.in0(A[29]), .in1(A[31]), .out(C[29]), .sel(Bit_1));
  Multiplexer multiplexer_4 (.in0(A[28]), .in1(A[30]), .out(C[28]), .sel(Bit_1));
  Multiplexer multiplexer_5 (.in0(A[27]), .in1(A[29]), .out(C[27]), .sel(Bit_1));
  Multiplexer multiplexer_6 (.in0(A[26]), .in1(A[28]), .out(C[26]), .sel(Bit_1));
  Multiplexer multiplexer_7 (.in0(A[25]), .in1(A[27]), .out(C[25]), .sel(Bit_1));
  Multiplexer multiplexer_8 (.in0(A[24]), .in1(A[26]), .out(C[24]), .sel(Bit_1));
  Multiplexer multiplexer_9 (.in0(A[23]), .in1(A[25]), .out(C[23]), .sel(Bit_1));
  Multiplexer multiplexer_10 (.in0(A[22]), .in1(A[24]), .out(C[22]), .sel(Bit_1));
  Multiplexer multiplexer_11 (.in0(A[21]), .in1(A[23]), .out(C[21]), .sel(Bit_1));
  Multiplexer multiplexer_12 (.in0(A[20]), .in1(A[22]), .out(C[20]), .sel(Bit_1));
  Multiplexer multiplexer_13 (.in0(A[19]), .in1(A[21]), .out(C[19]), .sel(Bit_1));
  Multiplexer multiplexer_14 (.in0(A[18]), .in1(A[20]), .out(C[18]), .sel(Bit_1));
  Multiplexer multiplexer_15 (.in0(A[17]), .in1(A[19]), .out(C[17]), .sel(Bit_1));
  Multiplexer multiplexer_16 (.in0(A[16]), .in1(A[18]), .out(C[16]), .sel(Bit_1));
  Multiplexer multiplexer_17 (.in0(A[15]), .in1(A[17]), .out(C[15]), .sel(Bit_1));
  Multiplexer multiplexer_18 (.in0(A[14]), .in1(A[16]), .out(C[14]), .sel(Bit_1));
  Multiplexer multiplexer_19 (.in0(A[13]), .in1(A[15]), .out(C[13]), .sel(Bit_1));
  Multiplexer multiplexer_20 (.in0(A[12]), .in1(A[14]), .out(C[12]), .sel(Bit_1));
  Multiplexer multiplexer_21 (.in0(A[11]), .in1(A[13]), .out(C[11]), .sel(Bit_1));
  Multiplexer multiplexer_22 (.in0(A[10]), .in1(A[12]), .out(C[10]), .sel(Bit_1));
  Multiplexer multiplexer_23 (.in0(A[9]), .in1(A[11]), .out(C[9]), .sel(Bit_1));
  Multiplexer multiplexer_24 (.in0(A[8]), .in1(A[10]), .out(C[8]), .sel(Bit_1));
  Multiplexer multiplexer_25 (.in0(A[7]), .in1(A[9]), .out(C[7]), .sel(Bit_1));
  Multiplexer multiplexer_26 (.in0(A[6]), .in1(A[8]), .out(C[6]), .sel(Bit_1));
  Multiplexer multiplexer_27 (.in0(A[5]), .in1(A[7]), .out(C[5]), .sel(Bit_1));
  Multiplexer multiplexer_28 (.in0(A[4]), .in1(A[6]), .out(C[4]), .sel(Bit_1));
  Multiplexer multiplexer_29 (.in0(A[3]), .in1(A[5]), .out(C[3]), .sel(Bit_1));
  Multiplexer multiplexer_30 (.in0(A[2]), .in1(A[4]), .out(C[2]), .sel(Bit_1));
  Multiplexer multiplexer_31 (.in0(A[1]), .in1(A[3]), .out(C[1]), .sel(Bit_1));
  Multiplexer multiplexer_32 (.in0(A[0]), .in1(A[2]), .out(C[0]), .sel(Bit_1));

  // Other names for the same wires on the sheet: S = Bit_1
endmodule

module Shift_4bit_R (
  input  [31:0] A,
  input  Bit_2,
  output [31:0] C
);

  Multiplexer multiplexer_1 (.in0(A[31]), .in1(1'b0), .out(C[31]), .sel(Bit_2));
  Multiplexer multiplexer_2 (.in0(A[30]), .in1(1'b0), .out(C[30]), .sel(Bit_2));
  Multiplexer multiplexer_3 (.in0(A[29]), .in1(1'b0), .out(C[29]), .sel(Bit_2));
  Multiplexer multiplexer_4 (.in0(A[28]), .in1(1'b0), .out(C[28]), .sel(Bit_2));
  Multiplexer multiplexer_5 (.in0(A[27]), .in1(A[31]), .out(C[27]), .sel(Bit_2));
  Multiplexer multiplexer_6 (.in0(A[26]), .in1(A[30]), .out(C[26]), .sel(Bit_2));
  Multiplexer multiplexer_7 (.in0(A[25]), .in1(A[29]), .out(C[25]), .sel(Bit_2));
  Multiplexer multiplexer_8 (.in0(A[24]), .in1(A[28]), .out(C[24]), .sel(Bit_2));
  Multiplexer multiplexer_9 (.in0(A[23]), .in1(A[27]), .out(C[23]), .sel(Bit_2));
  Multiplexer multiplexer_10 (.in0(A[22]), .in1(A[26]), .out(C[22]), .sel(Bit_2));
  Multiplexer multiplexer_11 (.in0(A[21]), .in1(A[25]), .out(C[21]), .sel(Bit_2));
  Multiplexer multiplexer_12 (.in0(A[20]), .in1(A[24]), .out(C[20]), .sel(Bit_2));
  Multiplexer multiplexer_13 (.in0(A[19]), .in1(A[23]), .out(C[19]), .sel(Bit_2));
  Multiplexer multiplexer_14 (.in0(A[18]), .in1(A[22]), .out(C[18]), .sel(Bit_2));
  Multiplexer multiplexer_15 (.in0(A[17]), .in1(A[21]), .out(C[17]), .sel(Bit_2));
  Multiplexer multiplexer_16 (.in0(A[16]), .in1(A[20]), .out(C[16]), .sel(Bit_2));
  Multiplexer multiplexer_17 (.in0(A[15]), .in1(A[19]), .out(C[15]), .sel(Bit_2));
  Multiplexer multiplexer_18 (.in0(A[14]), .in1(A[18]), .out(C[14]), .sel(Bit_2));
  Multiplexer multiplexer_19 (.in0(A[13]), .in1(A[17]), .out(C[13]), .sel(Bit_2));
  Multiplexer multiplexer_20 (.in0(A[12]), .in1(A[16]), .out(C[12]), .sel(Bit_2));
  Multiplexer multiplexer_21 (.in0(A[11]), .in1(A[15]), .out(C[11]), .sel(Bit_2));
  Multiplexer multiplexer_22 (.in0(A[10]), .in1(A[14]), .out(C[10]), .sel(Bit_2));
  Multiplexer multiplexer_23 (.in0(A[9]), .in1(A[13]), .out(C[9]), .sel(Bit_2));
  Multiplexer multiplexer_24 (.in0(A[8]), .in1(A[12]), .out(C[8]), .sel(Bit_2));
  Multiplexer multiplexer_25 (.in0(A[7]), .in1(A[11]), .out(C[7]), .sel(Bit_2));
  Multiplexer multiplexer_26 (.in0(A[6]), .in1(A[10]), .out(C[6]), .sel(Bit_2));
  Multiplexer multiplexer_27 (.in0(A[5]), .in1(A[9]), .out(C[5]), .sel(Bit_2));
  Multiplexer multiplexer_28 (.in0(A[4]), .in1(A[8]), .out(C[4]), .sel(Bit_2));
  Multiplexer multiplexer_29 (.in0(A[3]), .in1(A[7]), .out(C[3]), .sel(Bit_2));
  Multiplexer multiplexer_30 (.in0(A[2]), .in1(A[6]), .out(C[2]), .sel(Bit_2));
  Multiplexer multiplexer_31 (.in0(A[1]), .in1(A[5]), .out(C[1]), .sel(Bit_2));
  Multiplexer multiplexer_32 (.in0(A[0]), .in1(A[4]), .out(C[0]), .sel(Bit_2));

  // Other names for the same wires on the sheet: S = Bit_2
endmodule

module Shift_8bit_R (
  input  [31:0] A,
  input  Bit_3,
  output [31:0] C
);

  Multiplexer multiplexer_1 (.in0(A[31]), .in1(1'b0), .out(C[31]), .sel(A[31]));
  Multiplexer multiplexer_2 (.in0(A[31]), .in1(1'b0), .out(C[30]), .sel(A[31]));
  Multiplexer multiplexer_3 (.in0(A[29]), .in1(1'b0), .out(C[29]), .sel(A[31]));
  Multiplexer multiplexer_4 (.in0(A[28]), .in1(1'b0), .out(C[28]), .sel(A[31]));
  Multiplexer multiplexer_5 (.in0(A[27]), .in1(1'b0), .out(C[27]), .sel(A[31]));
  Multiplexer multiplexer_6 (.in0(A[26]), .in1(1'b0), .out(C[26]), .sel(A[31]));
  Multiplexer multiplexer_7 (.in0(A[25]), .in1(1'b0), .out(C[25]), .sel(A[31]));
  Multiplexer multiplexer_8 (.in0(A[24]), .in1(1'b0), .out(C[24]), .sel(A[31]));
  Multiplexer multiplexer_9 (.in0(A[23]), .in1(A[31]), .out(C[23]), .sel(A[31]));
  Multiplexer multiplexer_10 (.in0(A[22]), .in1(A[31]), .out(C[22]), .sel(A[31]));
  Multiplexer multiplexer_11 (.in0(A[21]), .in1(A[29]), .out(C[21]), .sel(A[31]));
  Multiplexer multiplexer_12 (.in0(A[20]), .in1(A[28]), .out(C[20]), .sel(A[31]));
  Multiplexer multiplexer_13 (.in0(A[19]), .in1(A[27]), .out(C[19]), .sel(A[31]));
  Multiplexer multiplexer_14 (.in0(A[18]), .in1(A[26]), .out(C[18]), .sel(A[31]));
  Multiplexer multiplexer_15 (.in0(A[17]), .in1(A[25]), .out(C[17]), .sel(A[31]));
  Multiplexer multiplexer_16 (.in0(A[16]), .in1(A[24]), .out(C[16]), .sel(A[31]));
  Multiplexer multiplexer_17 (.in0(A[15]), .in1(A[23]), .out(C[15]), .sel(A[31]));
  Multiplexer multiplexer_18 (.in0(A[14]), .in1(A[22]), .out(C[14]), .sel(A[31]));
  Multiplexer multiplexer_19 (.in0(A[13]), .in1(A[21]), .out(C[13]), .sel(A[31]));
  Multiplexer multiplexer_20 (.in0(A[12]), .in1(A[20]), .out(C[12]), .sel(A[31]));
  Multiplexer multiplexer_21 (.in0(A[11]), .in1(A[19]), .out(C[11]), .sel(A[31]));
  Multiplexer multiplexer_22 (.in0(A[10]), .in1(A[18]), .out(C[10]), .sel(A[31]));
  Multiplexer multiplexer_23 (.in0(A[9]), .in1(A[17]), .out(C[9]), .sel(A[31]));
  Multiplexer multiplexer_24 (.in0(A[8]), .in1(A[16]), .out(C[8]), .sel(A[31]));
  Multiplexer multiplexer_25 (.in0(A[7]), .in1(A[15]), .out(C[7]), .sel(A[31]));
  Multiplexer multiplexer_26 (.in0(A[6]), .in1(A[14]), .out(C[6]), .sel(A[31]));
  Multiplexer multiplexer_27 (.in0(A[5]), .in1(A[13]), .out(C[5]), .sel(A[31]));
  Multiplexer multiplexer_28 (.in0(A[4]), .in1(A[12]), .out(C[4]), .sel(A[31]));
  Multiplexer multiplexer_29 (.in0(A[3]), .in1(A[11]), .out(C[3]), .sel(A[31]));
  Multiplexer multiplexer_30 (.in0(A[2]), .in1(A[10]), .out(C[2]), .sel(A[31]));
  Multiplexer multiplexer_31 (.in0(A[1]), .in1(A[9]), .out(C[1]), .sel(A[31]));
  Multiplexer multiplexer_32 (.in0(A[0]), .in1(A[8]), .out(C[0]), .sel(A[31]));

  assign A[30] = A[31];
  assign Bit_3 = A[31];

  // Other names for the same wires on the sheet: S = A[31]
endmodule

module Shift_16bit_R (
  input  [31:0] A,
  input  Bit_4,
  output [31:0] C
);

  Multiplexer multiplexer_1 (.in0(A[31]), .in1(1'b0), .out(C[31]), .sel(A[31]));
  Multiplexer multiplexer_2 (.in0(A[31]), .in1(1'b0), .out(C[30]), .sel(A[31]));
  Multiplexer multiplexer_3 (.in0(A[29]), .in1(1'b0), .out(C[29]), .sel(A[31]));
  Multiplexer multiplexer_4 (.in0(A[28]), .in1(1'b0), .out(C[28]), .sel(A[31]));
  Multiplexer multiplexer_5 (.in0(A[27]), .in1(1'b0), .out(C[27]), .sel(A[31]));
  Multiplexer multiplexer_6 (.in0(A[26]), .in1(1'b0), .out(C[26]), .sel(A[31]));
  Multiplexer multiplexer_7 (.in0(A[25]), .in1(1'b0), .out(C[25]), .sel(A[31]));
  Multiplexer multiplexer_8 (.in0(A[24]), .in1(1'b0), .out(C[24]), .sel(A[31]));
  Multiplexer multiplexer_9 (.in0(A[23]), .in1(1'b0), .out(C[23]), .sel(A[31]));
  Multiplexer multiplexer_10 (.in0(A[22]), .in1(1'b0), .out(C[22]), .sel(A[31]));
  Multiplexer multiplexer_11 (.in0(A[21]), .in1(1'b0), .out(C[21]), .sel(A[31]));
  Multiplexer multiplexer_12 (.in0(A[20]), .in1(1'b0), .out(C[20]), .sel(A[31]));
  Multiplexer multiplexer_13 (.in0(A[19]), .in1(1'b0), .out(C[19]), .sel(A[31]));
  Multiplexer multiplexer_14 (.in0(A[18]), .in1(1'b0), .out(C[18]), .sel(A[31]));
  Multiplexer multiplexer_15 (.in0(A[17]), .in1(1'b0), .out(C[17]), .sel(A[31]));
  Multiplexer multiplexer_16 (.in0(A[16]), .in1(1'b0), .out(C[16]), .sel(A[31]));
  Multiplexer multiplexer_17 (.in0(A[15]), .in1(A[31]), .out(C[15]), .sel(A[31]));
  Multiplexer multiplexer_18 (.in0(A[14]), .in1(A[31]), .out(C[14]), .sel(A[31]));
  Multiplexer multiplexer_19 (.in0(A[13]), .in1(A[29]), .out(C[13]), .sel(A[31]));
  Multiplexer multiplexer_20 (.in0(A[12]), .in1(A[28]), .out(C[12]), .sel(A[31]));
  Multiplexer multiplexer_21 (.in0(A[11]), .in1(A[27]), .out(C[11]), .sel(A[31]));
  Multiplexer multiplexer_22 (.in0(A[10]), .in1(A[26]), .out(C[10]), .sel(A[31]));
  Multiplexer multiplexer_23 (.in0(A[9]), .in1(A[25]), .out(C[9]), .sel(A[31]));
  Multiplexer multiplexer_24 (.in0(A[8]), .in1(A[24]), .out(C[8]), .sel(A[31]));
  Multiplexer multiplexer_25 (.in0(A[7]), .in1(A[23]), .out(C[7]), .sel(A[31]));
  Multiplexer multiplexer_26 (.in0(A[6]), .in1(A[22]), .out(C[6]), .sel(A[31]));
  Multiplexer multiplexer_27 (.in0(A[5]), .in1(A[21]), .out(C[5]), .sel(A[31]));
  Multiplexer multiplexer_28 (.in0(A[4]), .in1(A[20]), .out(C[4]), .sel(A[31]));
  Multiplexer multiplexer_29 (.in0(A[3]), .in1(A[19]), .out(C[3]), .sel(A[31]));
  Multiplexer multiplexer_30 (.in0(A[2]), .in1(A[18]), .out(C[2]), .sel(A[31]));
  Multiplexer multiplexer_31 (.in0(A[1]), .in1(A[17]), .out(C[1]), .sel(A[31]));
  Multiplexer multiplexer_32 (.in0(A[0]), .in1(A[16]), .out(C[0]), .sel(A[31]));

  assign A[30] = A[31];
  assign Bit_4 = A[31];

  // Other names for the same wires on the sheet: S = A[31]
endmodule

module Full_Adder (
  input  C_in,
  input  A,
  input  B,
  output C_out,
  output S
);

  wire and_1_out, and_2_out, and_3_out, and_4_out, xor_1_out;

  and and_1 (and_1_out, C_in, A);
  and and_2 (and_2_out, A, B);
  and and_3 (and_3_out, C_in, B);
  and and_4 (and_4_out, C_in, A, B);
  ExactlyOne xor_1 (.out(xor_1_out), .in0(C_in), .in1(A), .in2(B));
  or or_1 (C_out, and_1_out, and_2_out, and_3_out);
  or or_2 (S, and_4_out, xor_1_out);
endmodule

module Adder_4bits_LA (
  input  C_in,
  input  [3:0] A,
  input  [3:0] B,
  output C_out,
  output [3:0] S
);

  wire full_adder_1_c_out, full_adder_1_s, full_adder_2_c_out, full_adder_2_s, full_adder_3_c_out,
       full_adder_3_s, full_adder_4_c_out, full_adder_4_s, full_adder_5_c_out, full_adder_5_s,
       full_adder_6_c_out, full_adder_6_s, full_adder_7_c_out, full_adder_7_s, full_adder_8_c_out,
       full_adder_8_s;

  Full_Adder full_adder_1 (.C_in(1'b0), .A(A[0]), .B(B[0]), .C_out(full_adder_1_c_out), .S(full_adder_1_s));
  Full_Adder full_adder_2 (.C_in(1'b1), .A(A[0]), .B(B[0]), .C_out(full_adder_2_c_out), .S(full_adder_2_s));
  Multiplexer multiplexer_1 (.in0(full_adder_1_s), .in1(full_adder_2_s), .out(S[0]), .sel(C_in));
  Full_Adder full_adder_3 (
    .C_in(full_adder_1_c_out), .A(A[1]), .B(B[1]), .C_out(full_adder_3_c_out), .S(full_adder_3_s));
  Full_Adder full_adder_4 (
    .C_in(full_adder_2_c_out), .A(A[1]), .B(B[1]), .C_out(full_adder_4_c_out), .S(full_adder_4_s));
  Multiplexer multiplexer_2 (.in0(full_adder_3_s), .in1(full_adder_4_s), .out(S[1]), .sel(C_in));
  Full_Adder full_adder_5 (
    .C_in(full_adder_3_c_out), .A(A[2]), .B(B[2]), .C_out(full_adder_5_c_out), .S(full_adder_5_s));
  Full_Adder full_adder_6 (
    .C_in(full_adder_4_c_out), .A(A[2]), .B(B[2]), .C_out(full_adder_6_c_out), .S(full_adder_6_s));
  Multiplexer multiplexer_3 (.in0(full_adder_5_s), .in1(full_adder_6_s), .out(S[2]), .sel(C_in));
  Full_Adder full_adder_7 (
    .C_in(full_adder_5_c_out), .A(A[3]), .B(B[3]), .C_out(full_adder_7_c_out), .S(full_adder_7_s));
  Full_Adder full_adder_8 (
    .C_in(full_adder_6_c_out), .A(A[3]), .B(B[3]), .C_out(full_adder_8_c_out), .S(full_adder_8_s));
  Multiplexer multiplexer_4 (.in0(full_adder_7_c_out), .in1(full_adder_8_c_out), .out(C_out), .sel(C_in));
  Multiplexer multiplexer_5 (.in0(full_adder_7_s), .in1(full_adder_8_s), .out(S[3]), .sel(C_in));

  // Other names for the same wires on the sheet: Seletor = C_in
endmodule

module IP (
  input  [31:0] A,
  input  Clock,
  output [31:0] S
);

  Register #(.width(32)) register_1 (.D(A), .en(1'b1), .clk(Clock), .Q(S));  // open: clr
endmodule

module Mem_Controle (
  input  [3:0] Op,
  output ULA_mux,
  output [2:0] ULA,
  output Reg_WE,
  output Disp,
  output IP
);

  wire and_1_out, and_2_out, and_3_out, and_4_out, and_5_out, and_6_out, and_7_out, and_8_out, and_9_out,
       and_10_out, and_11_out, and_12_out, or_1_out, or_2_out, or_3_out, or_4_out, or_5_out, xnor_1_out,
       xor_1_out;

  or or_1 (or_1_out, Op[1], Op[0]);
  and and_1 (and_1_out, Op[3], Op[2], Op[1], Op[0]);
  or or_2 (or_2_out, Op[2], Op[1]);
  and and_2 (and_2_out, Op[3], ~Op[2], ~Op[1]);  // AND_Gate
  and and_3 (and_3_out, Op[3], Op[2], Op[1], ~Op[0]);  // AND_Gate
  and and_4 (and_4_out, Op[3], ~Op[2], ~Op[1]);  // AND_Gate
  and and_5 (and_5_out, ~Op[3], ~Op[2], Op[1], Op[0]);  // AND_Gate
  or or_3 (or_3_out, Op[1], Op[0]);
  and and_6 (and_6_out, Op[3], ~Op[2], ~Op[0]);  // AND_Gate
  or or_4 (or_4_out, Op[1], Op[0]);
  xor xor_1 (xor_1_out, Op[3], Op[2]);
  and and_7 (and_7_out, Op[3], Op[2], Op[1], ~Op[0]);  // AND_Gate
  or or_5 (or_5_out, Op[1], Op[0]);
  and and_8 (and_8_out, Op[3], ~Op[2], or_1_out);  // AND_Gate
  and and_9 (and_9_out, ~Op[3], ~Op[0], or_2_out);  // AND_Gate
  and and_10 (and_10_out, ~Op[3], Op[2], xnor_1_out);  // AND_Gate
  xnor xnor_1 (xnor_1_out, Op[1], Op[0]);
  and and_11 (and_11_out, ~Op[3], Op[2], or_3_out);  // AND_Gate
  and and_12 (and_12_out, ~Op[3], ~Op[2], or_4_out);  // AND_Gate
  and and_13 (Disp, Op[3], Op[2], ~Op[1], ~Op[0]);  // AND_Gate
  and and_14 (IP, Op[3], Op[2], or_5_out);
  or or_6 (ULA_mux, and_8_out, and_1_out);
  or or_7 (ULA[0], and_9_out, and_2_out, and_3_out);
  or or_8 (ULA[1], and_10_out, and_4_out, and_5_out);
  or or_9 (ULA[2], and_11_out, and_6_out);
  or or_10 (Reg_WE, and_12_out, xor_1_out, and_7_out);
endmodule

module ext_16_32 (
  input  [15:0] in_1,
  output [31:0] out_2
);

  Multiplexer #(.width(16)) multiplexer_1 (.in0({16{1'b0}}), .in1({16{1'b1}}), .out(out_2[31:16]), .sel(in_1[15]));

  assign out_2[15:0] = in_1;
endmodule

module Branch (
  input  IP,
  input  Zero,
  input  Reg_WE,
  output out_4
);

  wire and_1_out;

  and and_1 (and_1_out, IP, Reg_WE);
  Multiplexer multiplexer_1 (.in0(IP), .in1(Zero), .out(out_4), .sel(and_1_out));
endmodule
