// Logisim project simd.circ as structural Verilog: 8 circuits, main circuit main
module main (
);

  wire br, clk, dec_1_p2, dec_1_p3, dec_1_p4, dec_1_p5, ld, mv, pc_ctl, reg_ctl, st, ula_1_is_zero;
  wire [1:0] multiplexer_1_out;
  wire [2:0] ula_ctl;
  wire [3:0] imm;
  wire [7:0] multiplexer_2_out, pc_1_out_4, ram_1_dout, rb_1_out_a, rb_1_out_b, rom_1_data, ula_1_ula_out;

  Clock clock_1 (.out(clk));
  Multiplexer #(.width(2)) multiplexer_1 (.in0(imm[1:0]), .in1(2'b01), .out(multiplexer_1_out), .sel(mv));
  ROM rom_1 (.addr(pc_1_out_4), .data(rom_1_data));
  pc pc_1 (.rb(rb_1_out_b), .ctl(pc_ctl), .clk(clk), .out_4(pc_1_out_4));
  rb rb_1 (
    .clk(clk), .r0({8{1'b0}}), .r_a(multiplexer_1_out), .r_b(imm[3:2]), .we(reg_ctl),
    .data(multiplexer_2_out), .out_a(rb_1_out_a), .out_b(rb_1_out_b));
  // dec dec_1: pin names not known; wires that end beside it: rom_1_data, dec_1_p2, dec_1_p3, dec_1_p4, dec_1_p5, {imm, mv, br, st, ld, reg_ctl, ula_ctl}
  and and_1 (pc_ctl, br, ula_1_is_zero);
  ula ula_1 (
    .clk(clk), .a(rb_1_out_a), .b(rb_1_out_b), .imm(imm), .ctl(ula_ctl), .is_zero(ula_1_is_zero),
    .ula_out(ula_1_ula_out));
  RAM ram_1 (.addr(rb_1_out_b), .we(st), .oe(1'b1), .clk(clk), .din(ula_1_ula_out), .dout(ram_1_dout));
  // vpe vpe_1: pin names not known; wires that end beside it: dec_1_p2, dec_1_p2, {8{1'b0}}
  // vpe vpe_2: pin names not known; wires that end beside it: dec_1_p3, 8'h1
  // vpe vpe_3: pin names not known; wires that end beside it: dec_1_p4, 8'h2
  // vpe vpe_4: pin names not known; wires that end beside it: dec_1_p5, 8'h3
  Multiplexer #(.width(8)) multiplexer_2 (.in0(ula_1_ula_out), .in1(ram_1_dout), .out(multiplexer_2_out), .sel(ld));

  // Other names for the same wires on the sheet: reg_a[1:0] = imm[1:0]; reg_b[1:0] = imm[3:2]
endmodule

module pc (
  input  [7:0] rb,
  input  ctl,
  input  clk,
  output [7:0] out_4
);

  wire [7:0] adder_1_out, multiplexer_1_out;

  Multiplexer #(.width(8)) multiplexer_1 (.in0(8'h1), .in1(rb), .out(multiplexer_1_out), .sel(ctl));
  Register register_1 (.D(adder_1_out), .en(1'b1), .clk(clk), .Q(out_4));  // open: clr
  Adder adder_1 (.a(out_4), .b(multiplexer_1_out), .out(adder_1_out));  // open: cin, cout
endmodule

module rb (
  input  clk,
  input  [7:0] r0,
  input  [1:0] r_a,
  input  [1:0] r_b,
  input  we,
  input  [7:0] data,
  output [7:0] out_a,
  output [7:0] out_b
);

  wire demultiplexer_1_out1, demultiplexer_1_out2, demultiplexer_1_out3;
  wire [7:0] register_1_q, register_2_q, register_3_q, register_4_q;

  Demultiplexer #(.select(2)) demultiplexer_1 (
    .out1(demultiplexer_1_out1), .out2(demultiplexer_1_out2), .out3(demultiplexer_1_out3), .in(we), .sel(r_a));  // open: out0
  Register register_1 (.D(r0), .en(1'b1), .clk(clk), .Q(register_1_q));  // open: clr
  Register register_2 (.D(data), .en(demultiplexer_1_out1), .clk(clk), .Q(register_2_q));  // open: clr
  Register register_3 (.D(data), .en(demultiplexer_1_out2), .clk(clk), .Q(register_3_q));  // open: clr
  Register register_4 (.D(data), .en(demultiplexer_1_out3), .clk(clk), .Q(register_4_q));  // open: clr
  Multiplexer #(.select(2), .width(8)) multiplexer_1 (
    .in0(register_1_q), .in1(register_2_q), .in2(register_3_q), .in3(register_4_q), .out(out_a), .sel(r_a));
  Multiplexer #(.select(2), .width(8)) multiplexer_2 (
    .in0(register_1_q), .in1(register_2_q), .in2(register_3_q), .in3(register_4_q), .out(out_b), .sel(r_b));

  // Other names for the same wires on the sheet: ra[1:0] = r_a; rb[1:0] = r_b
endmodule

module ula (
  input  clk,
  input  [7:0] a,
  input  [7:0] b,
  input  [3:0] imm,
  input  [2:0] ctl,
  output is_zero,
  output [7:0] ula_out
);

  wire comparator_1_eq;
  wire [7:0] adder_1_out, and_1_out, bit_extender_1_out, or_1_out, subtractor_1_out;

  Adder adder_1 (.a(a), .b(b), .out(adder_1_out));  // open: cin, cout
  Subtractor subtractor_1 (.a(a), .b(b), .out(subtractor_1_out));  // open: bin, bout
  assign and_1_out = a & b;  // AND_Gate and_1, 8 bits wide
  assign or_1_out = a | b;  // OR_Gate or_1, 8 bits wide
  Comparator comparator_1 (.a(a), .b({8{1'b0}}), .eq(comparator_1_eq));  // open: gt, lt
  assign bit_extender_1_out = {{7{comparator_1_eq}}, comparator_1_eq};  // Bit_Extender bit_extender_1
  Multiplexer #(.select(3), .width(8)) multiplexer_1 (
    .in0(a), .in1(adder_1_out), .in2(subtractor_1_out), .in3(and_1_out), .in4(or_1_out), .in5({imm, a[3:0]}),
    .in6({a[7:4], imm}), .in7(bit_extender_1_out), .out(ula_out), .sel(ctl));
  Comparator comparator_2 (.a(ula_out), .b({8{1'b0}}), .eq(is_zero));  // open: gt, lt
endmodule

module dec (
  input  [7:0] in_1,
  output [11:0] vpe0,
  output [11:0] vpe1,
  output [11:0] vpe2,
  output [11:0] vpe3,
  output [11:0] spe
);

  PLA #(.in_width(4), .out_width(8), .\table ("0000 00010000 # load\n0001 00101000 # store\n0010 10001101 # mvh\n0011 10001110 # mvl\n0100 00001001 # add\n0101 00001010 # sub\n0110 00001011 # and\n0111 01000111 # branch")) pla_1 (
    .in(in_1[3:0]), .out(spe[7:0]));

  assign spe[11:8] = in_1[7:4];
  assign vpe0 = {in_1[7:4], spe[7:0]};
  assign vpe1 = {in_1[7:4], spe[7:0]};
  assign vpe2 = {in_1[7:4], spe[7:0]};
  assign vpe3 = {in_1[7:4], spe[7:0]};
endmodule

module spe (
  input  [12:0] in_1,
  output vpe0,
  output vpe1,
  output vpe2,
  output vpe3,
  output pc
);

  wire clk;
  wire [1:0] multiplexer_1_out, undriven;
  wire [7:0] multiplexer_2_out, ram_1_dout, rb_1_out_a, rb_1_out_b, ula_1_ula_out;

  Multiplexer #(.width(2)) multiplexer_1 (.in0(in_1[10:9]), .in1(2'b01), .out(multiplexer_1_out), .sel(in_1[8]));
  rb rb_1 (
    .clk(clk), .r0({8{1'b0}}), .r_a(multiplexer_1_out), .r_b(undriven), .data(multiplexer_2_out),
    .out_a(rb_1_out_a), .out_b(rb_1_out_b));  // open: we
  ula ula_1 (
    .clk(clk), .a(rb_1_out_a), .b(rb_1_out_b), .imm(in_1[12:9]), .ctl(in_1[2:0]), .ula_out(ula_1_ula_out));  // open: is_zero
  RAM ram_1 (.addr(rb_1_out_b), .we(in_1[5]), .oe(1'b1), .clk(clk), .din(ula_1_ula_out), .dout(ram_1_dout));
  Multiplexer #(.width(8)) multiplexer_2 (
    .in0(ula_1_ula_out), .in1(ram_1_dout), .out(multiplexer_2_out), .sel(in_1[4]));

  // Other names for the same wires on the sheet: ula_ctl[2:0] = in_1[2:0]; reg_ctl = in_1[3]; ld = in_1[4];
  //   st = in_1[5]; pc_t = in_1[6]; br = in_1[7]; mv = in_1[8]; imm[3:0] = in_1[12:9]; ra[1:0] = in_1[10:9]
endmodule

module vpe (
  input  [11:0] op,
  input  [7:0] id,
  input  in_3,
  output out_4
);

  wire clk, undriven;
  wire [1:0] ctl_1_out_3, ctl_1_out_4;
  wire [7:0] multiplexer_1_out, ram_1_dout, rb_1_out_a, rb_1_out_b, ula_1_ula_out;

  ctl ctl_1 (.in_1(in_3), .in_2(undriven), .out_3(ctl_1_out_3), .out_4(ctl_1_out_4));
  rb rb_1 (
    .clk(clk), .r0(id), .r_a(ctl_1_out_3), .r_b(ctl_1_out_4), .we(op[3]), .data(multiplexer_1_out),
    .out_a(rb_1_out_a), .out_b(rb_1_out_b));
  ula ula_1 (
    .clk(clk), .a(rb_1_out_a), .b(rb_1_out_b), .imm(op[11:8]), .ctl(op[2:0]), .ula_out(ula_1_ula_out));  // open: is_zero
  RAM ram_1 (.addr(rb_1_out_b), .we(op[5]), .oe(1'b1), .clk(clk), .din(ula_1_ula_out), .dout(ram_1_dout));
  Multiplexer #(.width(8)) multiplexer_1 (.in0(ula_1_ula_out), .in1(ram_1_dout), .out(multiplexer_1_out), .sel(op[4]));

  // Other names for the same wires on the sheet: ula_ctl[2:0] = op[2:0]; reg_ctl = op[3]; ld = op[4]; st = op[5];
  //   br = op[6]; mv = op[7]; imm[3:0] = op[11:8]; reg_a[1:0] = op[9:8]; reg_b[1:0] = op[11:10]
endmodule

module ctl (
  input  in_1,
  input  in_2,
  output [1:0] out_3,
  output [1:0] out_4
);
endmodule
