// Logisim project sagui.circ as structural Verilog: 5 circuits, main circuit main
module main (
);

  wire branch, clk, isZero, load, pc_ctl, store;
  wire [1:0] control_out;
  wire [2:0] ula_ctl;
  wire [3:0] demultiplexer_1_out0, demultiplexer_1_out1;
  wire [7:0] multiplexer_1_out, pc_1_out_7, ram_1_dout, rb_1_out_a, rb_1_out_b, rom_1_data, ula_1_res;

  Clock clock_1 (.out(clk));
  ROM rom_1 (.addr(pc_1_out_7), .data(rom_1_data));
  pc pc_1 (
    .im(demultiplexer_1_out0), .rb(rb_1_out_b), .ctl(pc_ctl), .clk(clk), .Branch(branch), .isZero(isZero),
    .out_7(pc_1_out_7));
  Demultiplexer #(.width(4)) demultiplexer_1 (
    .out0(demultiplexer_1_out0), .out1(demultiplexer_1_out1), .in(rom_1_data[3:0]), .sel(control_out[0]));
  PLA #(.in_width(4), .out_width(9), .\table ("0000 001000001 # brzr\n0001 001000000 # brzi\n0010 001000001 # jr\n0011 001000000 # ji\n0100 010000001 # ld\n0101 000000001 # st\n0110 000000001 # movr\n0111 000000000 # movh\n1000 000000000 # movl\n1001 000000001 # add\n1000 000001001 # sub\n1011 000010001 # and\n1100 000011001 # or\n1101 000100001 # not\n1110 000101001 # slr\n1111 000110001 # srr")) control (
    .in(rom_1_data[7:4]), .out({branch, store, load, pc_ctl, ula_ctl, control_out}));
  rb rb_1 (
    .clk(clk), .r_a(demultiplexer_1_out1[1:0]), .r_b(demultiplexer_1_out1[3:2]), .we(control_out[1]),
    .data(multiplexer_1_out), .out_a(rb_1_out_a), .out_b(rb_1_out_b));
  ula ula_1 (.clk(clk), .a(rb_1_out_a), .b(rb_1_out_b), .ctl(ula_ctl), .isZero(isZero), .res(ula_1_res));
  RAM ram_1 (.addr(rb_1_out_b), .we(store), .oe(1'b1), .clk(clk), .din(ula_1_res), .dout(ram_1_dout));
  Multiplexer #(.width(8)) multiplexer_1 (.in0(ula_1_res), .in1(ram_1_dout), .out(multiplexer_1_out), .sel(load));
endmodule

module pc (
  input  [3:0] im,
  input  [7:0] rb,
  input  ctl,
  input  clk,
  input  Branch,
  input  isZero,
  output [7:0] out_7
);

  wire and_1_out;
  wire [7:0] adder_1_out, bit_extender_1_out, multiplexer_1_out, multiplexer_2_out;

  assign bit_extender_1_out = {{4{1'b0}}, im};  // Bit_Extender bit_extender_1
  and and_1 (and_1_out, Branch, isZero);
  Multiplexer #(.width(8)) multiplexer_1 (.in0(bit_extender_1_out), .in1(rb), .out(multiplexer_1_out), .sel(and_1_out));
  Multiplexer #(.width(8)) multiplexer_2 (.in0(8'h1), .in1(multiplexer_1_out), .out(multiplexer_2_out), .sel(ctl));
  Register register_1 (.D(adder_1_out), .en(1'b1), .clk(clk), .Q(out_7));  // open: clr
  Adder adder_1 (.a(out_7), .b(multiplexer_2_out), .out(adder_1_out));  // open: cin, cout
endmodule

module ctl (
  input  [3:0] op,
  output [1:0] rb,
  output rb_we,
  output [3:0] ula,
  output pc,
  output load,
  output store
);
endmodule

module rb (
  input  clk,
  input  [1:0] r_a,
  input  [1:0] r_b,
  input  we,
  input  [7:0] data,
  output [7:0] out_a,
  output [7:0] out_b
);

  wire demultiplexer_1_out0, demultiplexer_1_out1, demultiplexer_1_out2, demultiplexer_1_out3;
  wire [7:0] register_1_q, register_2_q, register_3_q, register_4_q;

  Demultiplexer #(.select(2)) demultiplexer_1 (
    .out0(demultiplexer_1_out0), .out1(demultiplexer_1_out1), .out2(demultiplexer_1_out2),
    .out3(demultiplexer_1_out3), .in(we), .sel(r_a));
  Register register_1 (.D(data), .en(demultiplexer_1_out0), .clk(clk), .Q(register_1_q));  // open: clr
  Register register_2 (.D(data), .en(demultiplexer_1_out1), .clk(clk), .Q(register_2_q));  // open: clr
  Register register_3 (.D(data), .en(demultiplexer_1_out2), .clk(clk), .Q(register_3_q));  // open: clr
  Register register_4 (.D(data), .en(demultiplexer_1_out3), .clk(clk), .Q(register_4_q));  // open: clr
  Multiplexer #(.select(2), .width(8)) multiplexer_1 (
    .in0(register_1_q), .in1(register_2_q), .in2(register_3_q), .in3(register_4_q), .out(out_a), .sel(r_a));
  Multiplexer #(.select(2), .width(8)) multiplexer_2 (
    .in0(register_1_q), .in1(register_2_q), .in2(register_3_q), .in3(register_4_q), .out(out_b), .sel(r_b));

  // Other names for the same wires on the sheet: ra[1:0] = r_a; rb[1:0] = r_b
endmodule

module ula (
  input  clk,
  input  [7:0] a,
  input  [7:0] b,
  input  [2:0] ctl,
  output isZero,
  output [7:0] res
);

  wire [7:0] adder_1_out, and_1_out, negator_1_out, or_1_out, shifter_1_out, shifter_2_out, subtractor_1_out;

  Adder adder_1 (.a(a), .b(b), .out(adder_1_out));  // open: cin, cout
  Subtractor subtractor_1 (.a(a), .b(b), .out(subtractor_1_out));  // open: bin, bout
  assign and_1_out = a & b;  // AND_Gate and_1, 8 bits wide
  assign or_1_out = a | b;  // OR_Gate or_1, 8 bits wide
  Negator negator_1 (.in(b), .out(negator_1_out));
  Shifter shifter_1 (.in(a), .\dist (b[2:0]), .out(shifter_1_out));
  Shifter #(.shift("lr")) shifter_2 (.in(a), .\dist (b[2:0]), .out(shifter_2_out));
  Multiplexer #(.select(3), .width(8)) multiplexer_1 (
    .in0(adder_1_out), .in1(subtractor_1_out), .in2(and_1_out), .in3(or_1_out), .in4(negator_1_out),
    .in5(shifter_1_out), .in6(shifter_2_out), .in7(a), .out(res), .sel(ctl));
  nor nor_1 (isZero, res[0], res[1], res[2], res[3], res[4], res[5], res[6], res[7]);
endmodule
